# Fritzing sketch 1-1 (saved by Fritzing 0.9.2b)
breadboards: 1

parts:
  부품1 = Arduino Uno (Rev3)
  LED1 = LED - 5mm [color="Green (570nm)" package="5 mm [THT]"]

nets:
  N1: 부품1.D5_PWM, LED1.anode
  N2: 부품1.GND, LED1.cathode
