# Fritzing sketch TrafficLight (saved by Fritzing 0.9.2b)
breadboards: 1

parts:
  부품1 = Arduino Uno (Rev3)
  LED1 = LED - 5mm [color="Red (633nm)" package="5 mm [THT]"]
  LED2 = LED - 5mm [color="Yellow (595nm)" package="5 mm [THT]"]
  R1 = Resistor [tolerance=±5% resistance=220 package=THT]
  R2 = Resistor [tolerance=±5% resistance=220 package=THT]
  LED3 = LED - 5mm [color="Green (555nm)" package="5 mm [THT]"]
  R3 = Resistor [tolerance=±5% resistance=220 package=THT]

nets:
  N1: 부품1.D10_PWM/SS, R3.Pin_1
  N2: 부품1.D11_PWM/MOSI, R2.Pin_1
  N3: 부품1.D12/MISO, R1.Pin_1
  N4: 부품1.GND, LED1.cathode, LED2.cathode, LED3.cathode
  N5: LED1.anode, R1.Pin_0
  N6: LED2.anode, R2.Pin_0
  N7: LED3.anode, R3.Pin_0
