# Fritzing sketch TrafficLight2 (saved by Fritzing 0.9.2b)
breadboards: 1

parts:
  부품1 = Arduino Uno (Rev3)
  LED3 = LED - 5mm [color="Green (555nm)" package="5 mm [THT]"]
  LED4 = LED - 5mm [color="Red (633nm)" package="5 mm [THT]"]
  LED5 = LED - 5mm [color="Green (555nm)" package="5 mm [THT]"]
  LED7 = LED - 5mm [color="Yellow (595nm)" package="5 mm [THT]"]
  R1 = Resistor [tolerance=±5% resistance=220 package=THT]
  R2 = Resistor [tolerance=±5% resistance=220 package=THT]
  R3 = Resistor [tolerance=±5% resistance=220 package=THT]
  R4 = Resistor [tolerance=±5% resistance=220 package=THT]
  R5 = Resistor [tolerance=±5% resistance=220 package=THT]
  LED8 = smd LED [color="Red (633nm)" package="1206 [SMD]"]

nets:
  N1: 부품1.D8, R5.Pin_1
  N2: 부품1.D10_PWM/SS, R3.Pin_1
  N3: 부품1.D11_PWM/MOSI, R2.Pin_1
  N4: 부품1.D12/MISO, R1.Pin_1
  N5: 부품1.GND, LED3.cathode, LED4.cathode, LED5.cathode, LED7.cathode, LED8.cathode
  N6: LED3.anode, R5.Pin_0
  N7: LED4.anode, R1.Pin_0
  N8: LED5.anode, R3.Pin_0
  N9: LED7.anode, R2.Pin_0
  N10: R4.Pin_0, LED8.anode
