# Fritzing sketch photoResistor_LED (saved by Fritzing 0.9.2b)
breadboards: 1

parts:
  부품1 = Arduino Uno (Rev3)
  R1 = Resistor [tolerance=±5% resistance=10 package="0603 [SMD]"]
  R2 = PHOTOCELL [package=photocell-kit]
  LED1 = smd LED [color="Blue (430nm)" package="1206 [SMD]"]
  R3 = Resistor [tolerance=±5% resistance=220 package="2512 [SMD]"]

nets:
  N1: 부품1.A0, R1.Pin_0, R2.P$2
  N2: 부품1.D13/SCK, R3.Pin_1
  N3: 부품1.5V, R1.Pin_1
  N4: 부품1.GND, R2.P$1, LED1.cathode
  N5: LED1.anode, R3.Pin_0
