# Fritzing sketch TrafficLight (saved by Fritzing 0.9.2b)
breadboards: 1

parts:
  부품1 = Arduino Uno (Rev3)
  LED1 = LED - 5mm [color="Red (633nm)" package="5 mm [THT]"]
  LED2 = LED - 5mm [color="Yellow (595nm)" package="5 mm [THT]"]
  LED3 = LED - 5mm [color="Green (565nm)" package="5 mm [THT]"]

nets:
  N1: 부품1.D10_PWM/SS, LED3.anode
  N2: 부품1.D11_PWM/MOSI, LED2.anode
  N3: 부품1.D12/MISO, LED1.anode
  N4: 부품1.GND, LED1.cathode, LED2.cathode, LED3.cathode
