# Fritzing sketch SignalLamp2 (saved by Fritzing 0.9.2b)
breadboards: 1

parts:
  부품1 = Arduino Uno (Rev3)
  LED3 = LED - 5mm [color="Green (570nm)" package="5 mm [THT]"]
  LED4 = LED - 5mm [color="Red (633nm)" package="5 mm [THT]"]
  LED5 = LED - 5mm [color="Green (570nm)" package="5 mm [THT]"]
  LED6 = LED - 5mm [color="Red (633nm)" package="5 mm [THT]"]
  LED7 = LED - 5mm [color="Yellow (595nm)" package="5 mm [THT]"]

nets:
  N1: 부품1.D8, LED5.anode
  N2: 부품1.D9_PWM, LED4.anode
  N3: 부품1.D10_PWM/SS, LED3.anode
  N4: 부품1.D11_PWM/MOSI, LED7.anode
  N5: 부품1.D12/MISO, LED6.anode
  N6: 부품1.GND, LED3.cathode, LED4.cathode, LED5.cathode, LED6.cathode, LED7.cathode
