# Fritzing sketch photoResistor (saved by Fritzing 0.9.2b)
breadboards: 1

parts:
  부품1 = Arduino Uno (Rev3)
  R1 = Resistor [tolerance=±5% resistance=10 package="0603 [SMD]"]
  R2 = PHOTOCELL [package=photocell-kit]

nets:
  N1: 부품1.A0, R1.Pin_0, R2.P$2
  N2: 부품1.5V, R1.Pin_1
  N3: 부품1.GND, R2.P$1
